# Fritzing sketch Temperature_Detection_Arduino_UNO (saved by Fritzing 0.9.3b)
breadboards: 1

parts:
  V1 = DC Power [voltage=5]  # not connected
  U1 = MLX90614 [package=to-39]
  Componente1 = Arduino Uno (Rev3) - ICSP
  LED4 = LED - 3mm [color="Red (633nm)" package="3 mm [THT]"]
  LED5 = LED - 3mm [color="Orange (605nm)" package="3 mm [THT]"]
  LED6 = LED - 3mm [color="Green (565nm)" package="3 mm [THT]"]
  R6 = Resistor [tolerance=±5% resistance=470 package=THT]
  R7 = Resistor [tolerance=±5% resistance=470 package=THT]
  R8 = Resistor [tolerance=±5% resistance=470 package=THT]
  R9 = Resistor [tolerance=±5% resistance=4.7k package=THT]
  R10 = Resistor [tolerance=±5% resistance=4.7k package=THT]
  hc-sr2 = hc-sr04
  LED7 = LED - 3mm [color="White (8000K)" package="3 mm [THT]"]
  LED8 = LED - 3mm [color="White (8000K)" package="3 mm [THT]"]
  LED9 = LED - 3mm [color="White (8000K)" package="3 mm [THT]"]
  R11 = Resistor [tolerance=±5% resistance=470 package=THT]
  R12 = Resistor [tolerance=±5% resistance=470 package=THT]
  R13 = Resistor [tolerance=±5% resistance=470 package=THT]

nets:
  N1: U1.SCL_VZ, Componente1.A5/SCL, R10.Pin_0
  N2: U1.PWM_SDA, Componente1.A4/SDA, R9.Pin_0
  VDD: U1.VDD, Componente1.3V3, R9.Pin_1, R10.Pin_1
  GND: U1.VSS, Componente1.GND, R6.Pin_1, R7.Pin_1, R8.Pin_1, hc-sr2.GND, R11.Pin_1, R12.Pin_1, R13.Pin_1
  N3: Componente1.D8, LED9.anode
  N4: Componente1.D9_PWM, LED8.anode
  N5: Componente1.D10_PWM/SS, LED7.anode
  N6: Componente1.D11_PWM/MOSI, LED6.anode
  N7: Componente1.D12/MISO, LED5.anode
  N8: Componente1.D13/SCK, LED4.anode
  N9: Componente1.D2, hc-sr2.Trig
  N10: Componente1.D3_PWM, hc-sr2.Echo
  5V: Componente1.5V, hc-sr2.VCC
  N11: LED4.cathode, R6.Pin_0
  N12: LED5.cathode, R7.Pin_0
  N13: LED6.cathode, R8.Pin_0
  N14: LED7.cathode, R12.Pin_0
  N15: LED8.cathode, R11.Pin_0
  N16: LED9.cathode, R13.Pin_0
